# Fritzing sketch MachDaoDong-Reset (saved by Fritzing 0.9.2b)
breadboards: 2

parts:
  PIC_16F877A1 = PIC 16F877A [package=THT]
  C1 = Capacitor [package=cap-pth-small2]
  C2 = Capacitor [package=cap-pth-small2]
  Y1 = CRYSTAL [package=hc49up]

nets:
  N1: PIC_16F877A1.OSC1/CLKIN, Y1.1
  N2: PIC_16F877A1.OSC2/CLKOUT, C2.1, Y1.2
  N3: C1.1, C2.2
